# Fritzing sketch prototype-board (saved by Fritzing 1.0.4)
breadboards: 1

parts:
  RHT1 = Humidity and Temperature Sensor RHT03
  LED1 = LED - 5mm [color="Red (633nm)" current=0.030A package="5 mm [THT]"]
  R2 = Resistor [tolerance=±5% power=0.25W resistance=10k package=THT]
  R3 = Resistor [tolerance=±5% power=0.25W resistance=220 package=THT]
  S1 = Reed switch [package=THT]
  R4 = Resistor [tolerance=±5% power=0.25W resistance=10k package=THT]
  U1 = ESP32S-HiLetgo [part_number=ESP32S-HiLetgo]

nets:
  VCC: RHT1.Vcc, R2.Pin_0, R4.Pin_0, U1.VIN
  N1: RHT1.Data-signal, R2.Pin_1, U1.GPIO26
  N2: RHT1.GND_2, S1.pin_2, U1.GPIO11
  N3: LED1.anode, R3.Pin_0
  N4: R3.Pin_1, U1.GPIO19
  N5: S1.pin_1, R4.Pin_1, U1.GPIO18

custom parts:
  ESP32S-HiLetgo: HiLetgo ESP-WROOM-32 ESP32 ESP-32S Development Board 2.4GHz Dual-Mode WiFi + Bluetooth Dual Cores Microcontroller The ESP32 integrated with Antenna switches, RF Balun, power amplifiers, low-noise amplifiers, filters, and management modules, and the entire solution occupies the least area of PCB. 2.4 GHz Wi-Fi plus Bluetooth dual-mode chip, with TSMC Ultra-low power consumption 40nm technology,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
