# Fritzing sketch through-hole-pcb (saved by Fritzing 1.0.4)
circuit board: 6.9431cm x 5.57251cm
perfboards: 1

parts:
  U1 = ESP32S-HiLetgo [part_number=ESP32S-HiLetgo]
  RHT1 = Humidity and Temperature Sensor RHT03
  S1 = SWITCH-MOMENTARY-2 [package=reed_switch_pth]
  LED1 = smd LED [color="Red (633nm)" package="0603 [SMD]"]
  R2 = Resistor [tolerance=±5% resistance=220 package="2010 [SMD]"]
  R4 = Resistor [tolerance=±5% resistance=220 package="2010 [SMD]"]
  LED2 = smd LED [color="Yellow (585nm)" package="0603 [SMD]"]
  R6 = Resistor [tolerance=±5% resistance=10k package="0402 [SMD]"]
  R7 = Resistor [tolerance=±5% resistance=10k package="0402 [SMD]"]
  LED3 = smd LED [color="Green (555nm)" package="0603 [SMD]"]
  R8 = Resistor [tolerance=±5% resistance=220 package="0402 [SMD]"]

nets:
  N1: U1.GPIO32, S1.2, R6.Pin_0
  N2: U1.GPIO25, R8.Pin_0
  N3: U1.GPIO27, R4.Pin_0
  N4: U1.GPIO12, R2.Pin_0
  N5: U1.GND, RHT1.GND_2, S1.1, LED1.cathode, LED2.cathode, LED3.cathode
  N6: U1.GPIO11, RHT1.Data-signal, R7.Pin_0
  VIN: U1.VIN, RHT1.Vcc, R6.Pin_1, R7.Pin_1
  N7: LED1.anode, R2.Pin_1
  N8: R4.Pin_1, LED2.anode
  N9: LED3.anode, R8.Pin_1

custom parts:
  ESP32S-HiLetgo: HiLetgo ESP-WROOM-32 ESP32 ESP-32S Development Board 2.4GHz Dual-Mode WiFi + Bluetooth Dual Cores Microcontroller The ESP32 integrated with Antenna switches, RF Balun, power amplifiers, low-noise amplifiers, filters, and management modules, and the entire solution occupies the least area of PCB. 2.4 GHz Wi-Fi plus Bluetooth dual-mode chip, with TSMC Ultra-low power consumption 40nm technology,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
